// Logisim project Mano_Basic_Computer.circ as structural Verilog: 35 circuits, main circuit main
module main (
  input  S_SET,
  input  FGO_SET,
  input  [7:0] INPR_IN,
  output [7:0] OUTR_OUT
);

  wire ac_controller_1_a_n_d, ac_controller_1_add, ac_controller_1_com, ac_controller_1_dr,
       ac_controller_1_inpr, ac_controller_1_shl, ac_controller_1_shr, ar_controller_1_ar_clr,
       ar_controller_1_ar_inc, ar_controller_1_ar_ld, B0, B1, B2, B3, B4, B5, B6, B7, B8, B9, B10, B11,
       bus_controller_1_s0, bus_controller_1_s1, bus_controller_1_s2, CLK, D0, D1, D2, D3, D4, D5, D6, D7,
       dr_controller_1_dr_clr, dr_controller_1_dr_inc, dr_controller_1_dr_ld, E, E_out, FGI, FGO, HLT, I,
       IEN, IR_15, ir_controller_1_ir_ld, or_1_out, outr_controller_1_outr_ld, pc_controller_1_pc_clr,
       pc_controller_1_pc_inc, pc_controller_1_pc_ld, R, S, sc_controller_1_sc_clr, sc_controller_1_sc_inc,
       T0, T1, T2, T3, T4, T5, T6, T7, T8, T9, T10, T11, T12, T13, T14, T15, tr_controller_1_tr_clr,
       tr_controller_1_tr_inc, tr_controller_1_tr_ld;
  wire [1:0] ac_controller_1_ac_clr, memory_controller_1_write;
  wire [3:0] Seq;
  wire [7:0] INPR_OUT;
  wire [11:0] Address;
  wire [14:12] IR_OUT;
  wire [15:0] AC_OUT, ALU_OUT, BUS_LINE, DR_OUT, Memory_OUT, PC_OUT, TR_OUT;
  wire [15:12] AR_OUT;

  Memory_Controller memory_controller_1 (
    .IR({IR_15, IR_OUT, B11, B10, B9, B8, B7, B6, B5, B4, B3, B2, B1, B0}), .Seq(Seq), .R(R),
    .Write(memory_controller_1_write[0]), .Read(memory_controller_1_write[1]));
  AR_Controller ar_controller_1 (
    .IR({IR_15, IR_OUT, B11, B10, B9, B8, B7, B6, B5, B4, B3, B2, B1, B0}), .Seq(Seq), .R(R),
    .AR_CLR(ar_controller_1_ar_clr), .AR_LD(ar_controller_1_ar_ld), .AR_INC(ar_controller_1_ar_inc));
  PC_Controller pc_controller_1 (
    .IR({IR_15, IR_OUT, B11, B10, B9, B8, B7, B6, B5, B4, B3, B2, B1, B0}), .Seq(Seq), .FGO(FGO), .FGI(FGI),
    .E(E), .R(R), .AC(AC_OUT), .DR(DR_OUT), .PC_CLR(pc_controller_1_pc_clr), .PC_LD(pc_controller_1_pc_ld),
    .PC_INC(pc_controller_1_pc_inc));
  DR_Controller dr_controller_1 (
    .IR({IR_15, IR_OUT, B11, B10, B9, B8, B7, B6, B5, B4, B3, B2, B1, B0}), .Seq(Seq),
    .DR_CLR(dr_controller_1_dr_clr), .DR_LD(dr_controller_1_dr_ld), .DR_INC(dr_controller_1_dr_inc));
  AC_Controller ac_controller_1 (
    .IR({IR_15, IR_OUT, B11, B10, B9, B8, B7, B6, B5, B4, B3, B2, B1, B0}), .Seq(Seq),
    .A_N_D(ac_controller_1_a_n_d), .ADD(ac_controller_1_add), .DR(ac_controller_1_dr),
    .INPR(ac_controller_1_inpr), .COM(ac_controller_1_com), .SHR(ac_controller_1_shr),
    .SHL(ac_controller_1_shl), .AC_CLR(ac_controller_1_ac_clr[0]), .AC_INC(ac_controller_1_ac_clr[1]));
  IR_Controller ir_controller_1 (.Seq(Seq), .R(R), .IR_LD(ir_controller_1_ir_ld));
  TR_Controller tr_controller_1 (
    .Seq(Seq), .R(R), .TR_CLR(tr_controller_1_tr_clr), .TR_LD(tr_controller_1_tr_ld),
    .TR_INC(tr_controller_1_tr_inc));
  OUTR_Controller outr_controller_1 (
    .IR({IR_15, IR_OUT, B11, B10, B9, B8, B7, B6, B5, B4, B3, B2, B1, B0}), .Seq(Seq),
    .OUTR_LD(outr_controller_1_outr_ld));
  RAM #(.addrWidth(12), .dataWidth(16), .trigger("high")) ram_1 (
    .addr(Address), .we(memory_controller_1_write[0]), .oe(memory_controller_1_write[1]), .din(BUS_LINE),
    .dout(Memory_OUT));
  or or_1 (or_1_out, ac_controller_1_a_n_d, ac_controller_1_add, ac_controller_1_dr, ac_controller_1_inpr, ac_controller_1_com, ac_controller_1_shr, ac_controller_1_shl);
  AR ar_1 (
    .CLR(ar_controller_1_ar_clr), .LD(ar_controller_1_ar_ld), .INC(ar_controller_1_ar_inc), .CLK(CLK),
    .BUS_IN(BUS_LINE), .BUS_OUT({AR_OUT, Address}));
  PC pc_1 (
    .CLR(pc_controller_1_pc_clr), .LD(pc_controller_1_pc_ld), .INC(pc_controller_1_pc_inc), .CLK(CLK),
    .BUS_IN(BUS_LINE), .BUS_OUT(PC_OUT));
  DR dr_1 (
    .CLR(dr_controller_1_dr_clr), .LD(dr_controller_1_dr_ld), .INC(dr_controller_1_dr_inc), .CLK(CLK),
    .BUS_IN(BUS_LINE), .BUS_OUT(DR_OUT));
  AC_register_sixteen ac_register_sixteen_1 (
    .DR_i(DR_OUT), .AC_i(AC_OUT), .From_INPR(INPR_OUT), .E_in(E), .A_N_D(ac_controller_1_a_n_d),
    .ADD(ac_controller_1_add), .DR(ac_controller_1_dr), .INPR(ac_controller_1_inpr),
    .COM(ac_controller_1_com), .SHR(ac_controller_1_shr), .SHL(ac_controller_1_shl), .E_out(E_out),
    .AC_out(ALU_OUT));
  AC ac_1 (
    .CLR(ac_controller_1_ac_clr[0]), .LD(or_1_out), .INC(ac_controller_1_ac_clr[1]), .CLK(CLK),
    .BUS_IN(ALU_OUT), .BUS_OUT(AC_OUT));
  INPR inpr_1 (.LD(1'b1), .CLK(CLK), .INPR_IN(INPR_IN), .INPR_OUT(INPR_OUT));
  IR ir_1 (
    .LD(ir_controller_1_ir_ld), .CLK(CLK), .BUS_IN(BUS_LINE),
    .BUS_OUT({IR_15, IR_OUT, B11, B10, B9, B8, B7, B6, B5, B4, B3, B2, B1, B0}));
  TR tr_1 (
    .CLR(tr_controller_1_tr_clr), .LD(tr_controller_1_tr_ld), .INC(tr_controller_1_tr_inc), .CLK(CLK),
    .BUS_IN(BUS_LINE), .BUS_OUT(TR_OUT));
  OUTR outr_1 (.LD(outr_controller_1_outr_ld), .CLK(CLK), .BUS_IN(BUS_LINE), .OUTR_OUT(OUTR_OUT));
  Hex_Digit_Display hex_digit_display_1 (.value(Memory_OUT[15:12]));  // open: dp
  Hex_Digit_Display hex_digit_display_2 (.value(Address[11:8]));  // open: dp
  Hex_Digit_Display hex_digit_display_3 (.value(Address[11:8]));  // open: dp
  Hex_Digit_Display hex_digit_display_4 (.value(AR_OUT));  // open: dp
  Hex_Digit_Display hex_digit_display_5 (.value(PC_OUT[11:8]));  // open: dp
  Hex_Digit_Display hex_digit_display_6 (.value(PC_OUT[15:12]));  // open: dp
  Hex_Digit_Display hex_digit_display_7 (.value(DR_OUT[11:8]));  // open: dp
  Hex_Digit_Display hex_digit_display_8 (.value(DR_OUT[15:12]));  // open: dp
  Hex_Digit_Display hex_digit_display_9 (.value(AC_OUT[15:12]));  // open: dp
  Hex_Digit_Display hex_digit_display_10 (.value({B11, B10, B9, B8}));  // open: dp
  Hex_Digit_Display hex_digit_display_11 (.value({IR_15, IR_OUT}));  // open: dp
  Hex_Digit_Display hex_digit_display_12 (.value(TR_OUT[11:8]));  // open: dp
  Hex_Digit_Display hex_digit_display_13 (.value(TR_OUT[15:12]));  // open: dp
  Hex_Digit_Display hex_digit_display_14 (.value(Memory_OUT[11:8]));  // open: dp
  Hex_Digit_Display hex_digit_display_15 (.value(Memory_OUT[7:4]));  // open: dp
  Hex_Digit_Display hex_digit_display_16 (.value(Address[7:4]));  // open: dp
  Hex_Digit_Display hex_digit_display_17 (.value(Address[3:0]));  // open: dp
  Hex_Digit_Display hex_digit_display_18 (.value(Address[7:4]));  // open: dp
  Hex_Digit_Display hex_digit_display_19 (.value(Address[3:0]));  // open: dp
  Hex_Digit_Display hex_digit_display_20 (.value(PC_OUT[7:4]));  // open: dp
  Hex_Digit_Display hex_digit_display_21 (.value(PC_OUT[3:0]));  // open: dp
  Hex_Digit_Display hex_digit_display_22 (.value(DR_OUT[7:4]));  // open: dp
  Hex_Digit_Display hex_digit_display_23 (.value(DR_OUT[3:0]));  // open: dp
  Hex_Digit_Display hex_digit_display_24 (.value(AC_OUT[11:8]));  // open: dp
  Hex_Digit_Display hex_digit_display_25 (.value(AC_OUT[7:4]));  // open: dp
  Hex_Digit_Display hex_digit_display_26 (.value({B7, B6, B5, B4}));  // open: dp
  Hex_Digit_Display hex_digit_display_27 (.value({B3, B2, B1, B0}));  // open: dp
  Hex_Digit_Display hex_digit_display_28 (.value(TR_OUT[7:4]));  // open: dp
  Hex_Digit_Display hex_digit_display_29 (.value(TR_OUT[3:0]));  // open: dp
  Hex_Digit_Display hex_digit_display_30 (.value(Memory_OUT[3:0]));  // open: dp
  Hex_Digit_Display hex_digit_display_31 (.value(AC_OUT[3:0]));  // open: dp
  SC_Controller sc_controller_1 (
    .IR({IR_15, IR_OUT, B11, B10, B9, B8, B7, B6, B5, B4, B3, B2, B1, B0}), .Seq(Seq), .R(R),
    .SC_CLR(sc_controller_1_sc_clr), .SC_INC(sc_controller_1_sc_inc));
  // Probe on R
  // Probe on S
  // Probe on IEN
  // Probe on FGO
  // Probe on FGI
  // Probe on E
  // Probe on I
  R_Controller r_controller_1 (.Seq(Seq), .IEN(IEN), .FGO(FGO), .FGI(FGI), .CLK(CLK), .R(R));
  S_Controller s_controller_1 (
    .IR({IR_15, IR_OUT, B11, B10, B9, B8, B7, B6, B5, B4, B3, B2, B1, B0}), .Seq(Seq), .SET(S_SET),
    .CLK(HLT), .S(S));
  IEN_Controller ien_controller_1 (
    .IR({IR_15, IR_OUT, B11, B10, B9, B8, B7, B6, B5, B4, B3, B2, B1, B0}), .Seq(Seq), .R(R), .CLK(CLK),
    .IEN(IEN));
  FGO_Controller fgo_controller_1 (
    .IR({IR_15, IR_OUT, B11, B10, B9, B8, B7, B6, B5, B4, B3, B2, B1, B0}), .Seq(Seq), .SET(FGO_SET),
    .CLK(CLK), .FGO(FGO));
  FGI_Controller fgi_controller_1 (
    .IR({IR_15, IR_OUT, B11, B10, B9, B8, B7, B6, B5, B4, B3, B2, B1, B0}), .Seq(Seq), .CLK(CLK),
    .INPR_IN(INPR_OUT), .FGI(FGI));
  E_Controller e_controller_1 (
    .IR({IR_15, IR_OUT, B11, B10, B9, B8, B7, B6, B5, B4, B3, B2, B1, B0}), .Seq(Seq), .E_out(E_out),
    .AC(AC_OUT), .CLK(CLK), .E(E));
  I_Controller i_controller_1 (.IR_15(IR_15), .CLK(CLK), .Indirect(I));
  BUS_Controller bus_controller_1 (
    .IR({IR_15, IR_OUT, B11, B10, B9, B8, B7, B6, B5, B4, B3, B2, B1, B0}), .Seq(Seq), .R(R),
    .S0(bus_controller_1_s0), .S1(bus_controller_1_s1), .S2(bus_controller_1_s2));
  // Probe on Seq
  SC sc_1 (.CLR(sc_controller_1_sc_clr), .INC(sc_controller_1_sc_inc), .CLK(CLK), .Seq(Seq));
  BUS_MUX bus_mux_1 (
    .Memory(Memory_OUT), .AR({AR_OUT, Address}), .PC(PC_OUT), .DR(DR_OUT), .AC(AC_OUT),
    .IR({IR_15, IR_OUT, B11, B10, B9, B8, B7, B6, B5, B4, B3, B2, B1, B0}), .TR(TR_OUT),
    .S0(bus_controller_1_s0), .S1(bus_controller_1_s1), .S2(bus_controller_1_s2), .BUS_LINE(BUS_LINE));
  Clock clock_1 (.out(HLT));
  Decoder #(.select(3)) decoder_1 (
    .out0(D0), .out1(D1), .out2(D2), .out3(D3), .out4(D4), .out5(D5), .out6(D6), .out7(D7), .sel(IR_OUT));  // open: en
  Decoder #(.select(4)) decoder_2 (
    .out0(T0), .out1(T1), .out2(T2), .out3(T3), .out4(T4), .out5(T5), .out6(T6), .out7(T7), .out8(T8),
    .out9(T9), .out10(T10), .out11(T11), .out12(T12), .out13(T13), .out14(T14), .out15(T15), .sel(Seq));  // open: en
  and and_1 (CLK, HLT, S);
  Hex_Digit_Display hex_digit_display_32 (.value(BUS_LINE[15:12]));  // open: dp
  Hex_Digit_Display hex_digit_display_33 (.value(BUS_LINE[11:8]));  // open: dp
  Hex_Digit_Display hex_digit_display_34 (.value(BUS_LINE[7:4]));  // open: dp
  Hex_Digit_Display hex_digit_display_35 (.value(BUS_LINE[3:0]));  // open: dp
  // also tied to GND on the sheet: {AR_OUT[12], AR_OUT[13], AR_OUT[14], AR_OUT[15]}

  // Other names for the same wires on the sheet: IR_OUT (some bits) = {IR_15, B11, B10, B9, B8, B7, B6, B5, B4, B3, B2, B1, B0};
  //   AR_OUT[11:0] = Address

  // Notes on the sheet:
  //   COMMON_BUS_SYSTEM
  //   SC
  //   Flip_Flop
  //   BUS_Controller
  //   Signal_Check
  //   Clock
endmodule

module fourbit (
  input  Clear,
  input  Load,
  input  Increment_count,
  input  [3:0] four_In,
  input  clock,
  output [3:0] four_Out,
  output output_carry
);

  wire and_1_out, and_2_out, and_3_out, and_4_out, and_5_out, and_6_out, and_7_out, and_8_out, and_9_out,
       and_10_out, and_11_out, and_12_out, and_13_out, not_1_out, not_2_out, not_3_out, not_4_out, not_5_out,
       not_6_out, or_1_out, or_2_out, or_3_out, or_4_out, or_5_out, or_6_out, or_7_out, or_8_out;

  not not_1 (not_1_out, Clear);
  not not_2 (not_2_out, Load);
  not not_3 (not_3_out, four_In[0]);
  not not_4 (not_4_out, four_In[1]);
  not not_5 (not_5_out, four_In[2]);
  not not_6 (not_6_out, four_In[3]);
  and and_1 (and_1_out, not_1_out, Load);
  and and_2 (and_2_out, not_1_out, not_2_out, Increment_count);
  and and_3 (and_3_out, and_1_out, four_In[0]);
  and and_4 (and_4_out, and_1_out, not_3_out);
  and and_5 (and_5_out, and_1_out, four_In[1]);
  and and_6 (and_6_out, and_1_out, not_4_out);
  and and_7 (and_7_out, and_1_out, four_In[2]);
  and and_8 (and_8_out, and_1_out, not_5_out);
  and and_9 (and_9_out, and_1_out, four_In[3]);
  and and_10 (and_10_out, and_1_out, not_6_out);
  and and_11 (and_11_out, and_2_out, four_Out[0]);
  and and_12 (and_12_out, and_11_out, four_Out[1]);
  and and_13 (and_13_out, and_12_out, four_Out[2]);
  or or_1 (or_1_out, and_2_out, and_3_out);
  or or_2 (or_2_out, Clear, and_2_out, and_4_out);
  or or_3 (or_3_out, and_11_out, and_5_out);
  or or_4 (or_4_out, Clear, and_11_out, and_6_out);
  or or_5 (or_5_out, and_12_out, and_7_out);
  or or_6 (or_6_out, Clear, and_12_out, and_8_out);
  or or_7 (or_7_out, and_13_out, and_9_out);
  or or_8 (or_8_out, Clear, and_13_out, and_10_out);
  J_K_Flip_Flop j_k_ff_1 (.J(or_1_out), .K(or_2_out), .clk(clock), .Q(four_Out[0]));  // open: Qn, preset, reset
  J_K_Flip_Flop j_k_ff_2 (.J(or_3_out), .K(or_4_out), .clk(clock), .Q(four_Out[1]));  // open: Qn, preset, reset
  J_K_Flip_Flop j_k_ff_3 (.J(or_5_out), .K(or_6_out), .clk(clock), .Q(four_Out[2]));  // open: Qn, preset, reset
  J_K_Flip_Flop j_k_ff_4 (.J(or_7_out), .K(or_8_out), .clk(clock), .Q(four_Out[3]));  // open: Qn, preset, reset
  and and_14 (output_carry, four_Out[3], and_13_out);
endmodule

module eightbit (
  input  clear,
  input  load,
  input  increment,
  input  clock,
  input  [7:0] eight_in,
  output [7:0] eight_out
);

  wire fourbit_1_output_carry;

  fourbit fourbit_1 (
    .Clear(clear), .Load(load), .Increment_count(increment), .four_In(eight_in[3:0]), .clock(clock),
    .four_Out(eight_out[3:0]), .output_carry(fourbit_1_output_carry));
  fourbit fourbit_2 (
    .Clear(clear), .Load(load), .Increment_count(fourbit_1_output_carry), .four_In(eight_in[7:4]),
    .clock(clock), .four_Out(eight_out[7:4]));  // open: output_carry
endmodule

module twelvebit (
  input  clear,
  input  load,
  input  increment,
  input  clock,
  input  [11:0] twelve_in,
  output [11:0] twelve_out
);

  wire fourbit_1_output_carry, fourbit_2_output_carry;

  fourbit fourbit_1 (
    .Clear(clear), .Load(load), .Increment_count(increment), .four_In(twelve_in[3:0]), .clock(clock),
    .four_Out(twelve_out[3:0]), .output_carry(fourbit_1_output_carry));
  fourbit fourbit_2 (
    .Clear(clear), .Load(load), .Increment_count(fourbit_1_output_carry), .four_In(twelve_in[7:4]),
    .clock(clock), .four_Out(twelve_out[7:4]), .output_carry(fourbit_2_output_carry));
  fourbit fourbit_3 (
    .Clear(clear), .Load(load), .Increment_count(fourbit_2_output_carry), .four_In(twelve_in[11:8]),
    .clock(clock), .four_Out(twelve_out[11:8]));  // open: output_carry
endmodule

module sixteenbit (
  input  clear,
  input  load,
  input  increment,
  input  clock,
  input  [15:0] sixteen_in,
  output [15:0] sixteen_out
);

  wire fourbit_1_output_carry, fourbit_2_output_carry, fourbit_3_output_carry;

  fourbit fourbit_1 (
    .Clear(clear), .Load(load), .Increment_count(increment), .four_In(sixteen_in[3:0]), .clock(clock),
    .four_Out(sixteen_out[3:0]), .output_carry(fourbit_1_output_carry));
  fourbit fourbit_2 (
    .Clear(clear), .Load(load), .Increment_count(fourbit_1_output_carry), .four_In(sixteen_in[7:4]),
    .clock(clock), .four_Out(sixteen_out[7:4]), .output_carry(fourbit_2_output_carry));
  fourbit fourbit_3 (
    .Clear(clear), .Load(load), .Increment_count(fourbit_2_output_carry), .four_In(sixteen_in[11:8]),
    .clock(clock), .four_Out(sixteen_out[11:8]), .output_carry(fourbit_3_output_carry));
  fourbit fourbit_4 (
    .Clear(clear), .Load(load), .Increment_count(fourbit_3_output_carry), .four_In(sixteen_in[15:12]),
    .clock(clock), .four_Out(sixteen_out[15:12]));  // open: output_carry
endmodule

module DR (
  input  CLR,
  input  LD,
  input  INC,
  input  CLK,
  input  [15:0] BUS_IN,
  output [15:0] BUS_OUT
);

  sixteenbit sixteenbit_1 (
    .clear(CLR), .load(LD), .increment(INC), .clock(CLK), .sixteen_in(BUS_IN), .sixteen_out(BUS_OUT));
endmodule

module AR (
  input  CLR,
  input  LD,
  input  INC,
  input  CLK,
  input  [15:0] BUS_IN,
  output [15:0] BUS_OUT
);

  twelvebit twelvebit_1 (
    .clear(CLR), .load(LD), .increment(INC), .clock(CLK), .twelve_in(BUS_IN[11:0]), .twelve_out(BUS_OUT[11:0]));

  assign BUS_OUT[15:12] = 4'b0000;
  // also tied to GND on the sheet: {BUS_IN[12], BUS_IN[13], BUS_IN[14], BUS_IN[15]}
endmodule

module AC (
  input  CLR,
  input  LD,
  input  INC,
  input  CLK,
  input  [15:0] BUS_IN,
  output [15:0] BUS_OUT
);

  sixteenbit sixteenbit_1 (
    .clear(CLR), .load(LD), .increment(INC), .clock(CLK), .sixteen_in(BUS_IN), .sixteen_out(BUS_OUT));
endmodule

module IR (
  input  LD,
  input  CLK,
  input  [15:0] BUS_IN,
  output [15:0] BUS_OUT
);

  sixteenbit sixteenbit_1 (
    .load(LD), .clock(CLK), .sixteen_in(BUS_IN), .sixteen_out(BUS_OUT));  // open: clear, increment
endmodule

module PC (
  input  CLR,
  input  LD,
  input  INC,
  input  CLK,
  input  [15:0] BUS_IN,
  output [15:0] BUS_OUT
);

  twelvebit twelvebit_1 (
    .clear(CLR), .load(LD), .increment(INC), .clock(CLK), .twelve_in(BUS_IN[11:0]), .twelve_out(BUS_OUT[11:0]));

  assign BUS_OUT[15:12] = 4'b0000;
  // also tied to GND on the sheet: {BUS_IN[12], BUS_IN[13], BUS_IN[14], BUS_IN[15]}
endmodule

module TR (
  input  CLR,
  input  LD,
  input  INC,
  input  CLK,
  input  [15:0] BUS_IN,
  output [15:0] BUS_OUT
);

  sixteenbit sixteenbit_1 (
    .clear(CLR), .load(LD), .increment(INC), .clock(CLK), .sixteen_in(BUS_IN), .sixteen_out(BUS_OUT));
endmodule

module INPR (
  input  LD,
  input  CLK,
  input  [7:0] INPR_IN,
  output [7:0] INPR_OUT
);

  eightbit eightbit_1 (.load(LD), .clock(CLK), .eight_in(INPR_IN), .eight_out(INPR_OUT));  // open: clear, increment
endmodule

module OUTR (
  input  LD,
  input  CLK,
  input  [15:0] BUS_IN,
  output [7:0] OUTR_OUT
);

  eightbit eightbit_1 (.load(LD), .clock(CLK), .eight_in(BUS_IN[7:0]), .eight_out(OUTR_OUT));  // open: clear, increment
  // also tied to GND on the sheet: {BUS_IN[8], BUS_IN[9], BUS_IN[10], BUS_IN[11], BUS_IN[12], BUS_IN[13], BUS_IN[14], BUS_IN[15]}
endmodule

module SC (
  input  CLR,
  input  INC,
  input  CLK,
  output [3:0] Seq
);

  Counter #(.max('hf), .width(4)) counter_1 (.load(CLR), .up(INC), .clk(CLK), .Q(Seq));  // open: clr, count, D, carry
endmodule

// AC 1bit
module AC_register (
  input  [6:0] INPUT_CONTROL_GATES,
  input  DR_i,
  input  AC_i,
  input  Ci,
  input  INPR_i,
  input  AC_i_plus_1,
  input  AC_i_minus_1,
  output AC_out,
  output Ci_plus_1
);

  wire A_N_D_out, ADD_out, adder_1_out, COM_out, DR_out, INPR_out, not_1_out, SHL_out, SHR_out;

  Adder #(.width(1)) adder_1 (.a(AC_i), .b(DR_i), .out(adder_1_out), .cin(Ci), .cout(Ci_plus_1));
  not not_1 (not_1_out, AC_i);
  and A_N_D (A_N_D_out, INPUT_CONTROL_GATES[6], AC_i, DR_i);
  and ADD (ADD_out, INPUT_CONTROL_GATES[5], adder_1_out);
  and DR (DR_out, INPUT_CONTROL_GATES[4], DR_i);
  and INPR (INPR_out, INPUT_CONTROL_GATES[3], INPR_i);
  and COM (COM_out, INPUT_CONTROL_GATES[2], not_1_out);
  and SHR (SHR_out, INPUT_CONTROL_GATES[1], AC_i_plus_1);
  and SHL (SHL_out, INPUT_CONTROL_GATES[0], AC_i_minus_1);
  or or_1 (AC_out, A_N_D_out, ADD_out, DR_out, INPR_out, COM_out, SHR_out, SHL_out);
endmodule

module AC_register_sixteen (
  input  [15:0] DR_i,
  input  [15:0] AC_i,
  input  [7:0] From_INPR,
  input  E_in,
  input  A_N_D,
  input  ADD,
  input  DR,
  input  INPR,
  input  COM,
  input  SHR,
  input  SHL,
  output E_out,
  output [15:0] AC_out
);

  wire ac_register_1_ci_plus_1, ac_register_2_ci_plus_1, ac_register_3_ci_plus_1, ac_register_4_ci_plus_1,
       ac_register_5_ci_plus_1, ac_register_6_ci_plus_1, ac_register_7_ci_plus_1, ac_register_8_ci_plus_1,
       ac_register_9_ci_plus_1, ac_register_10_ci_plus_1, ac_register_11_ci_plus_1, ac_register_12_ci_plus_1,
       ac_register_13_ci_plus_1, ac_register_14_ci_plus_1, ac_register_15_ci_plus_1, and_1_out, and_2_out,
       and_3_out, and_4_out, Carry_out, nor_1_out;

  nor nor_1 (nor_1_out, SHR, ADD, SHL);
  and and_1 (and_1_out, AC_i[15], SHL);
  and and_2 (and_2_out, AC_i[0], SHR);
  and and_3 (and_3_out, ADD, Carry_out);
  and and_4 (and_4_out, E_in, nor_1_out);
  or or_1 (E_out, and_1_out, and_2_out, and_3_out, and_4_out);
  AC_register ac_register_1 (
    .Ci(1'b0), .DR_i(DR_i[0]), .AC_i(AC_i[0]), .AC_i_plus_1(AC_i[1]), .AC_i_minus_1(E_in),
    .INPR_i(From_INPR[0]), .INPUT_CONTROL_GATES({A_N_D, ADD, DR, INPR, COM, SHR, SHL}), .AC_out(AC_out[0]),
    .Ci_plus_1(ac_register_1_ci_plus_1));
  AC_register ac_register_2 (
    .Ci(ac_register_1_ci_plus_1), .DR_i(DR_i[1]), .AC_i(AC_i[1]), .AC_i_plus_1(AC_i[2]),
    .AC_i_minus_1(AC_i[0]), .INPR_i(From_INPR[1]),
    .INPUT_CONTROL_GATES({A_N_D, ADD, DR, INPR, COM, SHR, SHL}), .AC_out(AC_out[1]),
    .Ci_plus_1(ac_register_2_ci_plus_1));
  AC_register ac_register_3 (
    .Ci(ac_register_2_ci_plus_1), .DR_i(DR_i[2]), .AC_i(AC_i[2]), .AC_i_plus_1(AC_i[3]),
    .AC_i_minus_1(AC_i[1]), .INPR_i(From_INPR[2]),
    .INPUT_CONTROL_GATES({A_N_D, ADD, DR, INPR, COM, SHR, SHL}), .AC_out(AC_out[2]),
    .Ci_plus_1(ac_register_3_ci_plus_1));
  AC_register ac_register_4 (
    .Ci(ac_register_3_ci_plus_1), .DR_i(DR_i[3]), .AC_i(AC_i[3]), .AC_i_plus_1(AC_i[4]),
    .AC_i_minus_1(AC_i[2]), .INPR_i(From_INPR[3]),
    .INPUT_CONTROL_GATES({A_N_D, ADD, DR, INPR, COM, SHR, SHL}), .AC_out(AC_out[3]),
    .Ci_plus_1(ac_register_4_ci_plus_1));
  AC_register ac_register_5 (
    .Ci(ac_register_4_ci_plus_1), .DR_i(DR_i[4]), .AC_i(AC_i[4]), .AC_i_plus_1(AC_i[5]),
    .AC_i_minus_1(AC_i[3]), .INPR_i(From_INPR[4]),
    .INPUT_CONTROL_GATES({A_N_D, ADD, DR, INPR, COM, SHR, SHL}), .AC_out(AC_out[4]),
    .Ci_plus_1(ac_register_5_ci_plus_1));
  AC_register ac_register_6 (
    .Ci(ac_register_5_ci_plus_1), .DR_i(DR_i[5]), .AC_i(AC_i[5]), .AC_i_plus_1(AC_i[6]),
    .AC_i_minus_1(AC_i[4]), .INPR_i(From_INPR[5]),
    .INPUT_CONTROL_GATES({A_N_D, ADD, DR, INPR, COM, SHR, SHL}), .AC_out(AC_out[5]),
    .Ci_plus_1(ac_register_6_ci_plus_1));
  AC_register ac_register_7 (
    .Ci(ac_register_6_ci_plus_1), .DR_i(DR_i[6]), .AC_i(AC_i[6]), .AC_i_plus_1(AC_i[7]),
    .AC_i_minus_1(AC_i[5]), .INPR_i(From_INPR[6]),
    .INPUT_CONTROL_GATES({A_N_D, ADD, DR, INPR, COM, SHR, SHL}), .AC_out(AC_out[6]),
    .Ci_plus_1(ac_register_7_ci_plus_1));
  AC_register ac_register_8 (
    .Ci(ac_register_7_ci_plus_1), .DR_i(DR_i[7]), .AC_i(AC_i[7]), .AC_i_plus_1(AC_i[8]),
    .AC_i_minus_1(AC_i[6]), .INPR_i(From_INPR[7]),
    .INPUT_CONTROL_GATES({A_N_D, ADD, DR, INPR, COM, SHR, SHL}), .AC_out(AC_out[7]),
    .Ci_plus_1(ac_register_8_ci_plus_1));
  AC_register ac_register_9 (
    .Ci(ac_register_8_ci_plus_1), .DR_i(DR_i[8]), .AC_i(AC_i[8]), .AC_i_plus_1(AC_i[9]),
    .AC_i_minus_1(AC_i[7]), .INPR_i(1'b0), .INPUT_CONTROL_GATES({A_N_D, ADD, DR, INPR, COM, SHR, SHL}),
    .AC_out(AC_out[8]), .Ci_plus_1(ac_register_9_ci_plus_1));
  AC_register ac_register_10 (
    .Ci(ac_register_9_ci_plus_1), .DR_i(DR_i[9]), .AC_i(AC_i[9]), .AC_i_plus_1(AC_i[10]),
    .AC_i_minus_1(AC_i[8]), .INPR_i(1'b0), .INPUT_CONTROL_GATES({A_N_D, ADD, DR, INPR, COM, SHR, SHL}),
    .AC_out(AC_out[9]), .Ci_plus_1(ac_register_10_ci_plus_1));
  AC_register ac_register_11 (
    .Ci(ac_register_10_ci_plus_1), .DR_i(DR_i[10]), .AC_i(AC_i[10]), .AC_i_plus_1(AC_i[11]),
    .AC_i_minus_1(AC_i[9]), .INPR_i(1'b0), .INPUT_CONTROL_GATES({A_N_D, ADD, DR, INPR, COM, SHR, SHL}),
    .AC_out(AC_out[10]), .Ci_plus_1(ac_register_11_ci_plus_1));
  AC_register ac_register_12 (
    .Ci(ac_register_11_ci_plus_1), .DR_i(DR_i[11]), .AC_i(AC_i[11]), .AC_i_plus_1(AC_i[12]),
    .AC_i_minus_1(AC_i[10]), .INPR_i(1'b0), .INPUT_CONTROL_GATES({A_N_D, ADD, DR, INPR, COM, SHR, SHL}),
    .AC_out(AC_out[11]), .Ci_plus_1(ac_register_12_ci_plus_1));
  AC_register ac_register_13 (
    .Ci(ac_register_12_ci_plus_1), .DR_i(DR_i[12]), .AC_i(AC_i[12]), .AC_i_plus_1(AC_i[13]),
    .AC_i_minus_1(AC_i[11]), .INPR_i(1'b0), .INPUT_CONTROL_GATES({A_N_D, ADD, DR, INPR, COM, SHR, SHL}),
    .AC_out(AC_out[12]), .Ci_plus_1(ac_register_13_ci_plus_1));
  AC_register ac_register_14 (
    .Ci(ac_register_13_ci_plus_1), .DR_i(DR_i[13]), .AC_i(AC_i[13]), .AC_i_plus_1(AC_i[14]),
    .AC_i_minus_1(AC_i[12]), .INPR_i(1'b0), .INPUT_CONTROL_GATES({A_N_D, ADD, DR, INPR, COM, SHR, SHL}),
    .AC_out(AC_out[13]), .Ci_plus_1(ac_register_14_ci_plus_1));
  AC_register ac_register_15 (
    .Ci(ac_register_14_ci_plus_1), .DR_i(DR_i[14]), .AC_i(AC_i[14]), .AC_i_plus_1(AC_i[15]),
    .AC_i_minus_1(AC_i[13]), .INPR_i(1'b0), .INPUT_CONTROL_GATES({A_N_D, ADD, DR, INPR, COM, SHR, SHL}),
    .AC_out(AC_out[14]), .Ci_plus_1(ac_register_15_ci_plus_1));
  AC_register ac_register_16 (
    .Ci(ac_register_15_ci_plus_1), .DR_i(DR_i[15]), .AC_i(AC_i[15]), .AC_i_plus_1(E_in),
    .AC_i_minus_1(AC_i[14]), .INPR_i(1'b0), .INPUT_CONTROL_GATES({A_N_D, ADD, DR, INPR, COM, SHR, SHL}),
    .AC_out(AC_out[15]), .Ci_plus_1(Carry_out));

  // Other names for the same wires on the sheet: INPR0 = From_INPR[0]; DR_0 = DR_i[0]; INPR1 = From_INPR[1];
  //   DR_1 = DR_i[1]; AC_0 = AC_i[0]; INPR2 = From_INPR[2]; DR_2 = DR_i[2]; AC_1 = AC_i[1]; INPR3 = From_INPR[3];
  //   DR_3 = DR_i[3]; AC_2 = AC_i[2]; INPR4 = From_INPR[4]; DR_4 = DR_i[4]; AC_3 = AC_i[3]; INPR5 = From_INPR[5];
  //   DR_5 = DR_i[5]; AC_4 = AC_i[4]; INPR6 = From_INPR[6]; DR_6 = DR_i[6]; AC_5 = AC_i[5]; INPR7 = From_INPR[7];
  //   DR_7 = DR_i[7]; AC_6 = AC_i[6]; DR_8 = DR_i[8]; AC_7 = AC_i[7]; DR_9 = DR_i[9]; AC_8 = AC_i[8];
  //   DR_10 = DR_i[10]; AC_9 = AC_i[9]; DR_11 = DR_i[11]; AC_10 = AC_i[10]; DR_12 = DR_i[12]; AC_11 = AC_i[11];
  //   DR_13 = DR_i[13]; AC_12 = AC_i[12]; DR_14 = DR_i[14]; AC_13 = AC_i[13]; DR_15 = DR_i[15]; AC_14 = AC_i[14];
  //   AC_15 = AC_i[15]; AC_out_0 = AC_out[0]; AC_out_1 = AC_out[1]; AC_out_2 = AC_out[2]; AC_out_3 = AC_out[3];
  //   AC_out_4 = AC_out[4]; AC_out_5 = AC_out[5]; AC_out_6 = AC_out[6]; AC_out_7 = AC_out[7]; AC_out_8 = AC_out[8];
  //   AC_out_9 = AC_out[9]; AC_out_10 = AC_out[10]; AC_out_11 = AC_out[11]; AC_out_12 = AC_out[12];
  //   AC_out_13 = AC_out[13]; AC_out_14 = AC_out[14]; AC_out_15 = AC_out[15];
  //   Control_Gates[6:0] = {A_N_D, ADD, DR, INPR, COM, SHR, SHL}
endmodule

module AR_Controller (
  input  [15:0] IR,
  input  [3:0] Seq,
  input  R,
  output AR_CLR,
  output AR_LD,
  output AR_INC
);

  wire and_2_out, and_3_out, and_4_out, D0, D1, D2, D3, D4, D5, D6, D7, not_1_out, not_2_out, not_3_out, T0,
       T1, T2, T3, T4, T5, T6, T7, T8, T9, T10, T11, T12, T13, T14, T15;

  Decoder #(.select(3)) decoder_1 (
    .out0(D0), .out1(D1), .out2(D2), .out3(D3), .out4(D4), .out5(D5), .out6(D6), .out7(D7), .sel(IR[14:12]));  // open: en
  Decoder #(.select(4)) decoder_2 (
    .out0(T0), .out1(T1), .out2(T2), .out3(T3), .out4(T4), .out5(T5), .out6(T6), .out7(T7), .out8(T8),
    .out9(T9), .out10(T10), .out11(T11), .out12(T12), .out13(T13), .out14(T14), .out15(T15), .sel(Seq));  // open: en
  not not_1 (not_1_out, D7);
  not not_2 (not_2_out, R);
  not not_3 (not_3_out, R);
  and and_1 (AR_CLR, R, T0);
  and and_2 (and_2_out, not_1_out, IR[15], T3);
  and and_3 (and_3_out, not_2_out, T2);
  and and_4 (and_4_out, not_3_out, T0);
  and and_5 (AR_INC, D5, T4);
  or or_1 (AR_LD, and_2_out, and_3_out, and_4_out);

  // Other names for the same wires on the sheet: B0 = IR[0]; B1 = IR[1]; B2 = IR[2]; B3 = IR[3]; B4 = IR[4];
  //   B5 = IR[5]; B6 = IR[6]; B7 = IR[7]; B8 = IR[8]; B9 = IR[9]; B10 = IR[10]; B11 = IR[11]; IR_15 = IR[15]
endmodule

module PC_Controller (
  input  [15:0] IR,
  input  [3:0] Seq,
  input  FGO,
  input  FGI,
  input  E,
  input  R,
  input  [15:0] AC,
  input  [15:0] DR,
  output PC_CLR,
  output PC_LD,
  output PC_INC
);

  wire AC_t, and_4_out, and_5_out, and_6_out, and_7_out, and_8_out, and_9_out, and_10_out, and_11_out,
       and_12_out, and_13_out, and_14_out, D0, D1, D2, D3, D4, D5, D6, D7, DR_t, not_1_out, not_2_out,
       not_3_out, not_4_out, not_5_out, not_6_out, p, r_t, T0, T1, T2, T3, T4, T5, T6, T7, T8, T9, T10, T11,
       T12, T13, T14, T15;

  not not_1 (not_1_out, IR[15]);
  Decoder #(.select(3)) decoder_1 (
    .out0(D0), .out1(D1), .out2(D2), .out3(D3), .out4(D4), .out5(D5), .out6(D6), .out7(D7), .sel(IR[14:12]));  // open: en
  Decoder #(.select(4)) decoder_2 (
    .out0(T0), .out1(T1), .out2(T2), .out3(T3), .out4(T4), .out5(T5), .out6(T6), .out7(T7), .out8(T8),
    .out9(T9), .out10(T10), .out11(T11), .out12(T12), .out13(T13), .out14(T14), .out15(T15), .sel(Seq));  // open: en
  and and_1 (p, D7, IR[15], T3);
  and and_2 (r_t, D7, not_1_out, T3);
  or or_1 (AC_t, AC[0], AC[1], AC[2], AC[3], AC[4], AC[5], AC[6], AC[7], AC[9], AC[10], AC[11], AC[12], AC[13], AC[14], AC[15], AC[8]);
  or or_2 (DR_t, DR[0], DR[1], DR[2], DR[3], DR[4], DR[5], DR[6], DR[7], DR[9], DR[10], DR[11], DR[12], DR[13], DR[14], DR[15], DR[8]);
  not not_2 (not_2_out, R);
  not not_3 (not_3_out, DR_t);
  and and_3 (PC_CLR, R, T1);
  and and_4 (and_4_out, D4, T4);
  and and_5 (and_5_out, D5, T5);
  and and_6 (and_6_out, not_2_out, T1);
  and and_7 (and_7_out, R, T2);
  and and_8 (and_8_out, D6, not_3_out, T6);
  not not_4 (not_4_out, AC[15]);
  and and_9 (and_9_out, r_t, not_4_out, IR[4]);
  and and_10 (and_10_out, r_t, AC[15], IR[3]);
  not not_5 (not_5_out, AC_t);
  not not_6 (not_6_out, E);
  or or_3 (PC_LD, and_4_out, and_5_out);
  and and_11 (and_11_out, r_t, not_5_out, IR[2]);
  and and_12 (and_12_out, r_t, not_6_out, IR[1]);
  and and_13 (and_13_out, p, FGI, IR[9]);
  and and_14 (and_14_out, p, FGO, IR[8]);
  or or_4 (PC_INC, and_6_out, and_7_out, and_8_out, and_9_out, and_10_out, and_11_out, and_12_out, and_13_out, and_14_out);

  // Other names for the same wires on the sheet: B0 = IR[0]; B1 = IR[1]; B2 = IR[2]; B3 = IR[3]; B4 = IR[4];
  //   B5 = IR[5]; B6 = IR[6]; B7 = IR[7]; B8 = IR[8]; B9 = IR[9]; B10 = IR[10]; B11 = IR[11]; AC_15 = AC[15];
  //   IR_15 = IR[15]
endmodule

module DR_Controller (
  input  [15:0] IR,
  input  [3:0] Seq,
  output DR_CLR,
  output DR_LD,
  output DR_INC
);

  wire and_1_out, and_2_out, and_3_out, and_4_out, D0, D1, D2, D3, D4, D5, D6, D7, T0, T1, T2, T3, T4, T5,
       T6, T7, T8, T9, T10, T11, T12, T13, T14, T15;

  Decoder #(.select(4)) decoder_1 (
    .out0(T0), .out1(T1), .out2(T2), .out3(T3), .out4(T4), .out5(T5), .out6(T6), .out7(T7), .out8(T8),
    .out9(T9), .out10(T10), .out11(T11), .out12(T12), .out13(T13), .out14(T14), .out15(T15), .sel(Seq));  // open: en
  Decoder #(.select(3)) decoder_2 (
    .out0(D0), .out1(D1), .out2(D2), .out3(D3), .out4(D4), .out5(D5), .out6(D6), .out7(D7), .sel(IR[14:12]));  // open: en
  and and_1 (and_1_out, D0, T4);
  and and_2 (and_2_out, D1, T4);
  and and_3 (and_3_out, D2, T4);
  and and_4 (and_4_out, D6, T4);
  and and_5 (DR_INC, D6, T5);
  or or_1 (DR_LD, and_1_out, and_2_out, and_3_out, and_4_out);

  assign DR_CLR = 1'b0;

  // Other names for the same wires on the sheet: B0 = IR[0]; B1 = IR[1]; B2 = IR[2]; B3 = IR[3]; B4 = IR[4];
  //   B5 = IR[5]; B6 = IR[6]; B7 = IR[7]; B8 = IR[8]; B9 = IR[9]; B10 = IR[10]; B11 = IR[11]; IR_15 = IR[15]
endmodule

module AC_Controller (
  input  [15:0] IR,
  input  [3:0] Seq,
  output A_N_D,
  output ADD,
  output DR,
  output INPR,
  output COM,
  output SHR,
  output SHL,
  output AC_CLR,
  output AC_INC
);

  wire D0, D1, D2, D3, D4, D5, D6, D7, not_1_out, p, r, T0, T1, T2, T3, T4, T5, T6, T7, T8, T9, T10, T11,
       T12, T13, T14, T15;

  not not_1 (not_1_out, IR[15]);
  Decoder #(.select(3)) decoder_1 (
    .out0(D0), .out1(D1), .out2(D2), .out3(D3), .out4(D4), .out5(D5), .out6(D6), .out7(D7), .sel(IR[14:12]));  // open: en
  Decoder #(.select(4)) decoder_2 (
    .out0(T0), .out1(T1), .out2(T2), .out3(T3), .out4(T4), .out5(T5), .out6(T6), .out7(T7), .out8(T8),
    .out9(T9), .out10(T10), .out11(T11), .out12(T12), .out13(T13), .out14(T14), .out15(T15), .sel(Seq));  // open: en
  and and_1 (p, D7, IR[15], T3);
  and and_2 (r, D7, not_1_out, T3);
  and and_3 (A_N_D, D0, T5);
  and and_4 (ADD, D1, T5);
  and and_5 (DR, D2, T5);
  and and_6 (INPR, p, IR[11]);
  and and_7 (COM, r, IR[9]);
  and and_8 (SHR, r, IR[7]);
  and and_9 (SHL, r, IR[6]);
  and and_10 (AC_CLR, r, IR[11]);
  and and_11 (AC_INC, r, IR[5]);

  // Other names for the same wires on the sheet: B0 = IR[0]; B1 = IR[1]; B2 = IR[2]; B3 = IR[3]; B4 = IR[4];
  //   B5 = IR[5]; B6 = IR[6]; B7 = IR[7]; B8 = IR[8]; B9 = IR[9]; B10 = IR[10]; B11 = IR[11]; IR_15 = IR[15]
endmodule

module IR_Controller (
  input  [3:0] Seq,
  input  R,
  output IR_LD
);

  wire not_1_out, T0, T1, T2, T3, T4, T5, T6, T7, T8, T9, T10, T11, T12, T13, T14, T15;

  Decoder #(.select(4)) decoder_1 (
    .out0(T0), .out1(T1), .out2(T2), .out3(T3), .out4(T4), .out5(T5), .out6(T6), .out7(T7), .out8(T8),
    .out9(T9), .out10(T10), .out11(T11), .out12(T12), .out13(T13), .out14(T14), .out15(T15), .sel(Seq));  // open: en
  not not_1 (not_1_out, R);
  and and_1 (IR_LD, not_1_out, T1);
endmodule

module TR_Controller (
  input  [3:0] Seq,
  input  R,
  output TR_CLR,
  output TR_LD,
  output TR_INC
);

  wire T0, T1, T2, T3, T4, T5, T6, T7, T8, T9, T10, T11, T12, T13, T14, T15;

  Decoder #(.select(4)) decoder_1 (
    .out0(T0), .out1(T1), .out2(T2), .out3(T3), .out4(T4), .out5(T5), .out6(T6), .out7(T7), .out8(T8),
    .out9(T9), .out10(T10), .out11(T11), .out12(T12), .out13(T13), .out14(T14), .out15(T15), .sel(Seq));  // open: en
  and and_1 (TR_LD, R, T0);

  assign TR_CLR = 1'b0;
  assign TR_INC = 1'b0;
endmodule

module OUTR_Controller (
  input  [15:0] IR,
  input  [3:0] Seq,
  output OUTR_LD
);

  wire D0, D1, D2, D3, D4, D5, D6, D7, p, T0, T1, T2, T3, T4, T5, T6, T7, T8, T9, T10, T11, T12, T13, T14,
       T15;

  Decoder #(.select(3)) decoder_1 (
    .out0(D0), .out1(D1), .out2(D2), .out3(D3), .out4(D4), .out5(D5), .out6(D6), .out7(D7), .sel(IR[14:12]));  // open: en
  Decoder #(.select(4)) decoder_2 (
    .out0(T0), .out1(T1), .out2(T2), .out3(T3), .out4(T4), .out5(T5), .out6(T6), .out7(T7), .out8(T8),
    .out9(T9), .out10(T10), .out11(T11), .out12(T12), .out13(T13), .out14(T14), .out15(T15), .sel(Seq));  // open: en
  and and_1 (p, D7, IR[15], T3);
  and and_2 (OUTR_LD, p, IR[10]);

  // Other names for the same wires on the sheet: B0 = IR[0]; B1 = IR[1]; B2 = IR[2]; B3 = IR[3]; B4 = IR[4];
  //   B5 = IR[5]; B6 = IR[6]; B7 = IR[7]; B8 = IR[8]; B9 = IR[9]; B10 = IR[10]; B11 = IR[11]; IR_15 = IR[15]
endmodule

module Memory_Controller (
  input  [15:0] IR,
  input  [3:0] Seq,
  input  R,
  output Write,
  output Read
);

  wire and_1_out, and_2_out, and_3_out, and_4_out, and_5_out, and_6_out, and_7_out, and_8_out, and_9_out,
       and_10_out, D0, D1, D2, D3, D4, D5, D6, D7, not_1_out, not_2_out, T0, T1, T2, T3, T4, T5, T6, T7, T8,
       T9, T10, T11, T12, T13, T14, T15;

  Decoder #(.select(3)) decoder_1 (
    .out0(D0), .out1(D1), .out2(D2), .out3(D3), .out4(D4), .out5(D5), .out6(D6), .out7(D7), .sel(IR[14:12]));  // open: en
  Decoder #(.select(4)) decoder_2 (
    .out0(T0), .out1(T1), .out2(T2), .out3(T3), .out4(T4), .out5(T5), .out6(T6), .out7(T7), .out8(T8),
    .out9(T9), .out10(T10), .out11(T11), .out12(T12), .out13(T13), .out14(T14), .out15(T15), .sel(Seq));  // open: en
  and and_1 (and_1_out, R, T1);
  and and_2 (and_2_out, D3, T4);
  not not_1 (not_1_out, R);
  and and_3 (and_3_out, not_1_out, T1);
  not not_2 (not_2_out, D7);
  and and_4 (and_4_out, not_2_out, IR[15], T3);
  and and_5 (and_5_out, D5, T4);
  and and_6 (and_6_out, D6, T6);
  and and_7 (and_7_out, D0, T4);
  and and_8 (and_8_out, D1, T4);
  and and_9 (and_9_out, D2, T4);
  and and_10 (and_10_out, D6, T4);
  or or_1 (Write, and_1_out, and_2_out, and_5_out, and_6_out);
  or or_2 (Read, and_3_out, and_4_out, and_7_out, and_8_out, and_9_out, and_10_out);

  // Other names for the same wires on the sheet: B0 = IR[0]; B1 = IR[1]; B2 = IR[2]; B3 = IR[3]; B4 = IR[4];
  //   B5 = IR[5]; B6 = IR[6]; B7 = IR[7]; B8 = IR[8]; B9 = IR[9]; B10 = IR[10]; B11 = IR[11]; IR_15 = IR[15]
endmodule

module SC_Controller (
  input  [15:0] IR,
  input  [3:0] Seq,
  input  R,
  output SC_CLR,
  output SC_INC
);

  wire and_3_out, and_4_out, and_5_out, and_6_out, and_7_out, and_8_out, and_9_out, and_10_out, D0, D1, D2,
       D3, D4, D5, D6, D7, not_1_out, p, r_t, T0, T1, T2, T3, T4, T5, T6, T7, T8, T9, T10, T11, T12, T13,
       T14, T15;

  not not_1 (not_1_out, IR[15]);
  Decoder #(.select(3)) decoder_1 (
    .out0(D0), .out1(D1), .out2(D2), .out3(D3), .out4(D4), .out5(D5), .out6(D6), .out7(D7), .sel(IR[14:12]));  // open: en
  Decoder #(.select(4)) decoder_2 (
    .out0(T0), .out1(T1), .out2(T2), .out3(T3), .out4(T4), .out5(T5), .out6(T6), .out7(T7), .out8(T8),
    .out9(T9), .out10(T10), .out11(T11), .out12(T12), .out13(T13), .out14(T14), .out15(T15), .sel(Seq));  // open: en
  and and_1 (p, D7, IR[15], T3);
  and and_2 (r_t, D7, not_1_out, T3);
  and and_3 (and_3_out, R, T2);
  and and_4 (and_4_out, D0, T5);
  and and_5 (and_5_out, D1, T5);
  and and_6 (and_6_out, D2, T5);
  and and_7 (and_7_out, D5, T5);
  and and_8 (and_8_out, D3, T4);
  and and_9 (and_9_out, D4, T4);
  and and_10 (and_10_out, D6, T6);
  or or_1 (SC_CLR, and_3_out, and_4_out, and_5_out, and_6_out, and_7_out, and_8_out, and_9_out, and_10_out, p, r_t);
  not not_2 (SC_INC, SC_CLR);

  // Other names for the same wires on the sheet: B0 = IR[0]; B1 = IR[1]; B2 = IR[2]; B3 = IR[3]; B4 = IR[4];
  //   B5 = IR[5]; B6 = IR[6]; B7 = IR[7]; B8 = IR[8]; B9 = IR[9]; B10 = IR[10]; B11 = IR[11]; IR_15 = IR[15]
endmodule

module R_Controller (
  input  [3:0] Seq,
  input  IEN,
  input  FGO,
  input  FGI,
  input  CLK,
  output R
);

  wire not_1_out, not_2_out, not_3_out, T0, T1, T2, T3, T4, T5, T6, T7, T8, T9, T10, T11, T12, T13, T14, T15;
  wire [1:0] and_1_out;
  wire [1:1] or_1_out;

  Decoder #(.select(4)) decoder_1 (
    .out0(T0), .out1(T1), .out2(T2), .out3(T3), .out4(T4), .out5(T5), .out6(T6), .out7(T7), .out8(T8),
    .out9(T9), .out10(T10), .out11(T11), .out12(T12), .out13(T13), .out14(T14), .out15(T15), .sel(Seq));  // open: en
  not not_1 (not_1_out, T0);
  not not_2 (not_2_out, T1);
  not not_3 (not_3_out, T2);
  or or_1 (or_1_out[1], FGI, FGO);
  and and_1 (and_1_out[0], not_1_out, not_2_out, not_3_out, IEN, or_1_out[1]);
  and and_2 (and_1_out[1], R, T2);
  J_K_Flip_Flop j_k_ff_1 (.J(and_1_out[0]), .K(and_1_out[1]), .clk(CLK), .Q(R));  // open: Qn, preset, reset
endmodule

module S_Controller (
  input  [15:0] IR,
  input  [3:0] Seq,
  input  SET,
  input  CLK,
  output S
);

  wire and_1_out, D0, D1, D2, D3, D4, D5, D6, D7, not_1_out, r, T0, T1, T2, T3, T4, T5, T6, T7, T8, T9, T10,
       T11, T12, T13, T14, T15;

  Decoder #(.select(3)) decoder_1 (
    .out0(D0), .out1(D1), .out2(D2), .out3(D3), .out4(D4), .out5(D5), .out6(D6), .out7(D7), .sel(IR[14:12]));  // open: en
  Decoder #(.select(4)) decoder_2 (
    .out0(T0), .out1(T1), .out2(T2), .out3(T3), .out4(T4), .out5(T5), .out6(T6), .out7(T7), .out8(T8),
    .out9(T9), .out10(T10), .out11(T11), .out12(T12), .out13(T13), .out14(T14), .out15(T15), .sel(Seq));  // open: en
  not not_1 (not_1_out, IR[15]);
  and and_1 (and_1_out, r, IR[0]);
  and and_2 (r, D7, not_1_out, T3);
  J_K_Flip_Flop j_k_ff_1 (.J(SET), .K(and_1_out), .clk(CLK), .Q(S));  // open: Qn, preset, reset

  // Other names for the same wires on the sheet: B0 = IR[0]; B1 = IR[1]; B2 = IR[2]; B3 = IR[3]; B4 = IR[4];
  //   B5 = IR[5]; B6 = IR[6]; B7 = IR[7]; B8 = IR[8]; B9 = IR[9]; B10 = IR[10]; B11 = IR[11]; IR_15 = IR[15]
endmodule

module IEN_Controller (
  input  [15:0] IR,
  input  [3:0] Seq,
  input  R,
  input  CLK,
  output IEN
);

  wire and_3_out, and_4_out, D0, D1, D2, D3, D4, D5, D6, D7, p, T0, T1, T2, T3, T4, T5, T6, T7, T8, T9, T10,
       T11, T12, T13, T14, T15;
  wire [1:0] and_2_out;

  Decoder #(.select(3)) decoder_1 (
    .out0(D0), .out1(D1), .out2(D2), .out3(D3), .out4(D4), .out5(D5), .out6(D6), .out7(D7), .sel(IR[14:12]));  // open: en
  Decoder #(.select(4)) decoder_2 (
    .out0(T0), .out1(T1), .out2(T2), .out3(T3), .out4(T4), .out5(T5), .out6(T6), .out7(T7), .out8(T8),
    .out9(T9), .out10(T10), .out11(T11), .out12(T12), .out13(T13), .out14(T14), .out15(T15), .sel(Seq));  // open: en
  and and_1 (p, D7, IR[15], T3);
  and and_2 (and_2_out[0], p, IR[7]);
  and and_3 (and_3_out, R, T2);
  and and_4 (and_4_out, p, IR[6]);
  or or_1 (and_2_out[1], and_3_out, and_4_out);
  J_K_Flip_Flop j_k_ff_1 (.J(and_2_out[0]), .K(and_2_out[1]), .clk(CLK), .Q(IEN));  // open: Qn, preset, reset

  // Other names for the same wires on the sheet: B0 = IR[0]; B1 = IR[1]; B2 = IR[2]; B3 = IR[3]; B4 = IR[4];
  //   B5 = IR[5]; B6 = IR[6]; B7 = IR[7]; B8 = IR[8]; B9 = IR[9]; B10 = IR[10]; B11 = IR[11]; IR_15 = IR[15]
endmodule

module FGO_Controller (
  input  [15:0] IR,
  input  [3:0] Seq,
  input  SET,
  input  CLK,
  output FGO
);

  wire and_2_out, D0, D1, D2, D3, D4, D5, D6, D7, p, T0, T1, T2, T3, T4, T5, T6, T7, T8, T9, T10, T11, T12,
       T13, T14, T15;

  Decoder #(.select(3)) decoder_1 (
    .out0(D0), .out1(D1), .out2(D2), .out3(D3), .out4(D4), .out5(D5), .out6(D6), .out7(D7), .sel(IR[14:12]));  // open: en
  Decoder #(.select(4)) decoder_2 (
    .out0(T0), .out1(T1), .out2(T2), .out3(T3), .out4(T4), .out5(T5), .out6(T6), .out7(T7), .out8(T8),
    .out9(T9), .out10(T10), .out11(T11), .out12(T12), .out13(T13), .out14(T14), .out15(T15), .sel(Seq));  // open: en
  and and_1 (p, D7, IR[15], T3);
  and and_2 (and_2_out, p, IR[10]);
  J_K_Flip_Flop j_k_ff_1 (.J(SET), .K(and_2_out), .clk(CLK), .Q(FGO));  // open: Qn, preset, reset

  // Other names for the same wires on the sheet: B0 = IR[0]; B1 = IR[1]; B2 = IR[2]; B3 = IR[3]; B4 = IR[4];
  //   B5 = IR[5]; B6 = IR[6]; B7 = IR[7]; B8 = IR[8]; B9 = IR[9]; B10 = IR[10]; B11 = IR[11]; IR_15 = IR[15]
endmodule

module FGI_Controller (
  input  [15:0] IR,
  input  [3:0] Seq,
  input  CLK,
  input  [7:0] INPR_IN,
  output FGI
);

  wire and_2_out, D0, D1, D2, D3, D4, D5, D6, D7, INPR, p, T0, T1, T2, T3, T4, T5, T6, T7, T8, T9, T10, T11,
       T12, T13, T14, T15;

  Decoder #(.select(3)) decoder_1 (
    .out0(D0), .out1(D1), .out2(D2), .out3(D3), .out4(D4), .out5(D5), .out6(D6), .out7(D7), .sel(IR[14:12]));  // open: en
  Decoder #(.select(4)) decoder_2 (
    .out0(T0), .out1(T1), .out2(T2), .out3(T3), .out4(T4), .out5(T5), .out6(T6), .out7(T7), .out8(T8),
    .out9(T9), .out10(T10), .out11(T11), .out12(T12), .out13(T13), .out14(T14), .out15(T15), .sel(Seq));  // open: en
  and and_1 (p, D7, IR[15], T3);
  and and_2 (and_2_out, p, IR[11]);
  J_K_Flip_Flop j_k_ff_1 (.J(INPR), .K(and_2_out), .clk(CLK), .Q(FGI));  // open: Qn, preset, reset
  or or_1 (INPR, INPR_IN[0], INPR_IN[1], INPR_IN[2], INPR_IN[3], INPR_IN[5], INPR_IN[6], INPR_IN[7], INPR_IN[4]);

  // Other names for the same wires on the sheet: B0 = IR[0]; B1 = IR[1]; B2 = IR[2]; B3 = IR[3]; B4 = IR[4];
  //   B5 = IR[5]; B6 = IR[6]; B7 = IR[7]; B8 = IR[8]; B9 = IR[9]; B10 = IR[10]; B11 = IR[11]; IR_15 = IR[15]
endmodule

module E_Controller (
  input  [15:0] IR,
  input  [3:0] Seq,
  input  E_out,
  input  [15:0] AC,
  input  CLK,
  output E
);

  wire and_1_out, and_2_out, and_3_out, and_4_out, and_5_out, and_6_out, and_7_out, and_8_out, and_9_out, D0,
       D1, D2, D3, D4, D5, D6, D7, not_1_out, not_2_out, not_3_out, r, T0, T1, T2, T3, T4, T5, T6, T7, T8,
       T9, T10, T11, T12, T13, T14, T15;
  wire [1:0] SET_out;

  and and_1 (and_1_out, r, IR[8]);
  and and_2 (and_2_out, r, IR[8]);
  not not_1 (not_1_out, AC[0]);
  not not_2 (not_2_out, AC[15]);
  Decoder #(.select(3)) decoder_1 (
    .out0(D0), .out1(D1), .out2(D2), .out3(D3), .out4(D4), .out5(D5), .out6(D6), .out7(D7), .sel(IR[14:12]));  // open: en
  Decoder #(.select(4)) decoder_2 (
    .out0(T0), .out1(T1), .out2(T2), .out3(T3), .out4(T4), .out5(T5), .out6(T6), .out7(T7), .out8(T8),
    .out9(T9), .out10(T10), .out11(T11), .out12(T12), .out13(T13), .out14(T14), .out15(T15), .sel(Seq));  // open: en
  not not_3 (not_3_out, IR[15]);
  and and_3 (and_3_out, D1, T5, E_out);
  and and_4 (and_4_out, r, IR[6], AC[15]);
  and and_5 (and_5_out, r, IR[7], AC[0]);
  and and_6 (and_6_out, r, IR[6], not_1_out);
  and and_7 (and_7_out, D1, T5, E_out);
  and and_8 (and_8_out, r, IR[7], not_2_out);
  and and_9 (and_9_out, r, IR[10]);
  and and_10 (r, D7, not_3_out, T3);
  or SET (SET_out[0], and_1_out, and_3_out, and_4_out, and_5_out);
  or RESET (SET_out[1], and_2_out, and_6_out, and_7_out, and_8_out, and_9_out);
  J_K_Flip_Flop j_k_ff_1 (.J(SET_out[0]), .K(SET_out[1]), .clk(CLK), .Q(E));  // open: Qn, preset, reset

  // Other names for the same wires on the sheet: B0 = IR[0]; B1 = IR[1]; B2 = IR[2]; B3 = IR[3]; B4 = IR[4];
  //   B5 = IR[5]; B6 = IR[6]; B7 = IR[7]; B8 = IR[8]; B9 = IR[9]; B10 = IR[10]; B11 = IR[11]; AC_0 = AC[0];
  //   AC_1 = AC[1]; AC_2 = AC[2]; AC_3 = AC[3]; AC_4 = AC[4]; AC_5 = AC[5]; AC_6 = AC[6]; AC_7 = AC[7]; AC_8 = AC[8];
  //   AC_9 = AC[9]; AC_10 = AC[10]; AC_11 = AC[11]; AC_12 = AC[12]; AC_13 = AC[13]; AC_14 = AC[14]; AC_15 = AC[15];
  //   IR_15 = IR[15]
endmodule

module BUS_MUX (
  input  [15:0] Memory,
  input  [15:0] AR,
  input  [15:0] PC,
  input  [15:0] DR,
  input  [15:0] AC,
  input  [15:0] IR,
  input  [15:0] TR,
  input  S0,
  input  S1,
  input  S2,
  output [15:0] BUS_LINE
);

  Multiplexer #(.select(3), .width(16)) multiplexer_1 (
    .in0({16{1'b0}}), .in1(AR), .in2(PC), .in3(DR), .in4(AC), .in5(IR), .in6(TR), .in7(Memory),
    .out(BUS_LINE), .sel({S2, S1, S0}));
endmodule

module BUS_Controller (
  input  [15:0] IR,
  input  [3:0] Seq,
  input  R,
  output S0,
  output S1,
  output S2
);

  wire and_3_out, and_4_out, and_5_out, and_6_out, and_7_out, and_8_out, and_9_out, and_10_out, and_11_out,
       and_14_out, and_15_out, and_16_out, and_17_out, and_18_out, and_19_out, D0, D1, D2, D3, D4, D5, D6,
       D7, not_1_out, not_2_out, not_3_out, not_4_out, not_5_out, p, r_t, T0, T1, T2, T3, T4, T5, T6, T7, T8,
       T9, T10, T11, T12, T13, T14, T15, X1, X2, X3, X4, X5, X6, X7;

  not not_1 (not_1_out, IR[15]);
  Decoder #(.select(3)) decoder_1 (
    .out0(D0), .out1(D1), .out2(D2), .out3(D3), .out4(D4), .out5(D5), .out6(D6), .out7(D7), .sel(IR[14:12]));  // open: en
  Decoder #(.select(4)) decoder_2 (
    .out0(T0), .out1(T1), .out2(T2), .out3(T3), .out4(T4), .out5(T5), .out6(T6), .out7(T7), .out8(T8),
    .out9(T9), .out10(T10), .out11(T11), .out12(T12), .out13(T13), .out14(T14), .out15(T15), .sel(Seq));  // open: en
  and and_1 (p, D7, IR[15], T3);
  and and_2 (r_t, D7, not_1_out, T3);
  not not_2 (not_2_out, R);
  and and_3 (and_3_out, D4, T4);
  and and_4 (and_4_out, D5, T5);
  and and_5 (and_5_out, not_2_out, T0);
  and and_6 (and_6_out, R, T0);
  and and_7 (and_7_out, D5, T4);
  and and_8 (and_8_out, D2, T5);
  and and_9 (and_9_out, D6, T6);
  or or_1 (X1, and_3_out, and_4_out);
  or or_2 (X2, and_5_out, and_6_out, and_7_out);
  or or_3 (X3, and_8_out, and_9_out);
  or or_4 (S0, X1, X3, X5, X7);
  or or_5 (S1, X2, X3, X6, X7);
  or or_6 (S2, X4, X5, X6, X7);
  not not_3 (not_3_out, R);
  not not_4 (not_4_out, R);
  and and_10 (and_10_out, D3, T4);
  and and_11 (and_11_out, p, IR[10]);
  and and_12 (X5, not_3_out, T2);
  and and_13 (X6, R, T1);
  and and_14 (and_14_out, not_4_out, T1);
  and and_15 (and_15_out, D0, T4);
  and and_16 (and_16_out, D1, T4);
  and and_17 (and_17_out, D2, T4);
  and and_18 (and_18_out, D6, T4);
  not not_5 (not_5_out, D7);
  and and_19 (and_19_out, not_5_out, IR[15], T3);
  or or_7 (X4, and_10_out, and_11_out);
  or or_8 (X7, and_14_out, and_15_out, and_16_out, and_17_out, and_18_out, and_19_out);

  // Other names for the same wires on the sheet: B0 = IR[0]; B1 = IR[1]; B2 = IR[2]; B3 = IR[3]; B4 = IR[4];
  //   B5 = IR[5]; B6 = IR[6]; B7 = IR[7]; B8 = IR[8]; B9 = IR[9]; B10 = IR[10]; B11 = IR[11]; IR_15 = IR[15]
endmodule

module back_up (
  input  S_SET,
  input  FGO_SET,
  input  [7:0] INPR_IN,
  output [7:0] OUTR_OUT
);

  wire ac_controller_1_a_n_d, ac_controller_1_add, ac_controller_1_com, ac_controller_1_dr,
       ac_controller_1_inpr, ac_controller_1_shl, ac_controller_1_shr, ar_controller_1_ar_clr,
       ar_controller_1_ar_inc, ar_controller_1_ar_ld, B0, B1, B2, B3, B4, B5, B6, B7, B8, B9, B10, B11, CLK,
       clock_1_out, D0, D1, D2, D3, D4, D5, D6, D7, dr_controller_1_dr_clr, dr_controller_1_dr_inc,
       dr_controller_1_dr_ld, E, E_out, FGI, FGO, IEN, IR_15, ir_controller_1_ir_ld, not_1_out, or_1_out,
       outr_controller_1_outr_ld, pc_controller_1_pc_clr, pc_controller_1_pc_inc, pc_controller_1_pc_ld, R,
       S, S0, S1, S2, sc_controller_1_sc_clr, sc_controller_1_sc_inc, T0, T1, T2, T3, T4, T5, T6, T7, T8, T9,
       T10, T11, T12, T13, T14, T15, tr_controller_1_tr_clr, tr_controller_1_tr_inc, tr_controller_1_tr_ld;
  wire [1:0] ac_controller_1_ac_clr, memory_controller_1_write;
  wire [3:0] Seq;
  wire [7:0] INPR_OUT;
  wire [11:0] Address;
  wire [14:12] IR_OUT;
  wire [15:0] AC_OUT, ALU_OUT, BUS_LINE, DR_OUT, Memory_OUT, PC_OUT, TR_OUT;
  wire [15:12] AR_OUT;

  Memory_Controller memory_controller_1 (
    .IR({IR_15, IR_OUT, B11, B10, B9, B8, B7, B6, B5, B4, B3, B2, B1, B0}), .Seq(Seq), .R(R),
    .Write(memory_controller_1_write[0]), .Read(memory_controller_1_write[1]));
  AR_Controller ar_controller_1 (
    .IR({IR_15, IR_OUT, B11, B10, B9, B8, B7, B6, B5, B4, B3, B2, B1, B0}), .Seq(Seq), .R(R),
    .AR_CLR(ar_controller_1_ar_clr), .AR_LD(ar_controller_1_ar_ld), .AR_INC(ar_controller_1_ar_inc));
  PC_Controller pc_controller_1 (
    .IR({IR_15, IR_OUT, B11, B10, B9, B8, B7, B6, B5, B4, B3, B2, B1, B0}), .Seq(Seq), .FGO(FGO), .FGI(FGI),
    .E(E), .R(R), .AC(AC_OUT), .DR(DR_OUT), .PC_CLR(pc_controller_1_pc_clr), .PC_LD(pc_controller_1_pc_ld),
    .PC_INC(pc_controller_1_pc_inc));
  DR_Controller dr_controller_1 (
    .IR({IR_15, IR_OUT, B11, B10, B9, B8, B7, B6, B5, B4, B3, B2, B1, B0}), .Seq(Seq),
    .DR_CLR(dr_controller_1_dr_clr), .DR_LD(dr_controller_1_dr_ld), .DR_INC(dr_controller_1_dr_inc));
  AC_Controller ac_controller_1 (
    .IR({IR_15, IR_OUT, B11, B10, B9, B8, B7, B6, B5, B4, B3, B2, B1, B0}), .Seq(Seq),
    .A_N_D(ac_controller_1_a_n_d), .ADD(ac_controller_1_add), .DR(ac_controller_1_dr),
    .INPR(ac_controller_1_inpr), .COM(ac_controller_1_com), .SHR(ac_controller_1_shr),
    .SHL(ac_controller_1_shl), .AC_CLR(ac_controller_1_ac_clr[0]), .AC_INC(ac_controller_1_ac_clr[1]));
  IR_Controller ir_controller_1 (.Seq(Seq), .R(R), .IR_LD(ir_controller_1_ir_ld));
  TR_Controller tr_controller_1 (
    .Seq(Seq), .R(R), .TR_CLR(tr_controller_1_tr_clr), .TR_LD(tr_controller_1_tr_ld),
    .TR_INC(tr_controller_1_tr_inc));
  OUTR_Controller outr_controller_1 (
    .IR({IR_15, IR_OUT, B11, B10, B9, B8, B7, B6, B5, B4, B3, B2, B1, B0}), .Seq(Seq),
    .OUTR_LD(outr_controller_1_outr_ld));
  or or_1 (or_1_out, ac_controller_1_a_n_d, ac_controller_1_add, ac_controller_1_dr, ac_controller_1_inpr, ac_controller_1_com, ac_controller_1_shr, ac_controller_1_shl);
  RAM #(.addrWidth(12), .dataWidth(16), .trigger("high")) ram_1 (
    .addr(Address), .we(memory_controller_1_write[0]), .oe(memory_controller_1_write[1]), .din(BUS_LINE),
    .dout(Memory_OUT));
  AR ar_1 (
    .CLR(ar_controller_1_ar_clr), .LD(ar_controller_1_ar_ld), .INC(ar_controller_1_ar_inc), .CLK(CLK),
    .BUS_IN(BUS_LINE), .BUS_OUT({AR_OUT, Address}));
  // Probe on {AR_OUT, Address}
  PC pc_1 (
    .CLR(pc_controller_1_pc_clr), .LD(pc_controller_1_pc_ld), .INC(pc_controller_1_pc_inc), .CLK(CLK),
    .BUS_IN(BUS_LINE), .BUS_OUT(PC_OUT));
  // Probe on PC_OUT
  DR dr_1 (
    .CLR(dr_controller_1_dr_clr), .LD(dr_controller_1_dr_ld), .INC(dr_controller_1_dr_inc), .CLK(CLK),
    .BUS_IN(BUS_LINE), .BUS_OUT(DR_OUT));
  // Probe on DR_OUT
  AC_register_sixteen ac_register_sixteen_1 (
    .DR_i(DR_OUT), .AC_i(AC_OUT), .From_INPR(INPR_OUT), .E_in(E), .A_N_D(ac_controller_1_a_n_d),
    .ADD(ac_controller_1_add), .DR(ac_controller_1_dr), .INPR(ac_controller_1_inpr),
    .COM(ac_controller_1_com), .SHR(ac_controller_1_shr), .SHL(ac_controller_1_shl), .E_out(E_out),
    .AC_out(ALU_OUT));
  // Probe on ALU_OUT
  AC ac_1 (
    .CLR(ac_controller_1_ac_clr[0]), .LD(or_1_out), .INC(ac_controller_1_ac_clr[1]), .CLK(CLK),
    .BUS_IN(ALU_OUT), .BUS_OUT(AC_OUT));
  // Probe on AC_OUT
  INPR inpr_1 (.LD(1'b1), .CLK(CLK), .INPR_IN(INPR_IN), .INPR_OUT(INPR_OUT));
  // Probe on INPR_OUT
  IR ir_1 (
    .LD(ir_controller_1_ir_ld), .CLK(CLK), .BUS_IN(BUS_LINE),
    .BUS_OUT({IR_15, IR_OUT, B11, B10, B9, B8, B7, B6, B5, B4, B3, B2, B1, B0}));
  // Probe on {IR_15, IR_OUT, B11, B10, B9, B8, B7, B6, B5, B4, B3, B2, B1, B0}
  TR tr_1 (
    .CLR(tr_controller_1_tr_clr), .LD(tr_controller_1_tr_ld), .INC(tr_controller_1_tr_inc), .CLK(CLK),
    .BUS_IN(BUS_LINE), .BUS_OUT(TR_OUT));
  // Probe on TR_OUT
  OUTR outr_1 (.LD(outr_controller_1_outr_ld), .CLK(CLK), .BUS_IN(BUS_LINE), .OUTR_OUT(OUTR_OUT));
  // Probe on OUTR_OUT
  // Probe on Address
  // Probe on Memory_OUT
  Clock clock_1 (.out(clock_1_out));
  not not_1 (not_1_out, S);
  and and_1 (CLK, clock_1_out, not_1_out);
  BUS_MUX bus_mux_1 (
    .Memory(Memory_OUT), .AR({AR_OUT, Address}), .PC(PC_OUT), .DR(DR_OUT), .AC(AC_OUT),
    .IR({IR_15, IR_OUT, B11, B10, B9, B8, B7, B6, B5, B4, B3, B2, B1, B0}), .TR(TR_OUT), .S0(S0), .S1(S1),
    .S2(S2), .BUS_LINE(BUS_LINE));
  // Probe on BUS_LINE
  SC_Controller sc_controller_1 (
    .IR({IR_15, IR_OUT, B11, B10, B9, B8, B7, B6, B5, B4, B3, B2, B1, B0}), .Seq(Seq), .R(R),
    .SC_CLR(sc_controller_1_sc_clr), .SC_INC(sc_controller_1_sc_inc));
  R_Controller r_controller_1 (.Seq(Seq), .IEN(IEN), .FGO(FGO), .FGI(FGI), .CLK(CLK), .R(R));
  // Probe on R
  S_Controller s_controller_1 (
    .IR({IR_15, IR_OUT, B11, B10, B9, B8, B7, B6, B5, B4, B3, B2, B1, B0}), .Seq(Seq), .SET(S_SET),
    .CLK(CLK), .S(S));
  // Probe on S
  IEN_Controller ien_controller_1 (
    .IR({IR_15, IR_OUT, B11, B10, B9, B8, B7, B6, B5, B4, B3, B2, B1, B0}), .Seq(Seq), .R(R), .CLK(CLK),
    .IEN(IEN));
  // Probe on IEN
  FGO_Controller fgo_controller_1 (
    .IR({IR_15, IR_OUT, B11, B10, B9, B8, B7, B6, B5, B4, B3, B2, B1, B0}), .Seq(Seq), .SET(FGO_SET),
    .CLK(CLK), .FGO(FGO));
  // Probe on FGO
  FGI_Controller fgi_controller_1 (
    .IR({IR_15, IR_OUT, B11, B10, B9, B8, B7, B6, B5, B4, B3, B2, B1, B0}), .Seq(Seq), .CLK(CLK),
    .INPR_IN(INPR_OUT), .FGI(FGI));
  // Probe on FGI
  E_Controller e_controller_1 (
    .IR({IR_15, IR_OUT, B11, B10, B9, B8, B7, B6, B5, B4, B3, B2, B1, B0}), .Seq(Seq), .E_out(E_out),
    .AC(AC_OUT), .CLK(CLK), .E(E));
  // Probe on E
  SC sc_1 (.CLR(sc_controller_1_sc_clr), .INC(sc_controller_1_sc_inc), .CLK(CLK), .Seq(Seq));
  // Probe on Seq
  Decoder #(.select(3)) decoder_1 (
    .out0(D0), .out1(D1), .out2(D2), .out3(D3), .out4(D4), .out5(D5), .out6(D6), .out7(D7), .sel(IR_OUT));  // open: en
  Decoder #(.select(4)) decoder_2 (
    .out0(T0), .out1(T1), .out2(T2), .out3(T3), .out4(T4), .out5(T5), .out6(T6), .out7(T7), .out8(T8),
    .out9(T9), .out10(T10), .out11(T11), .out12(T12), .out13(T13), .out14(T14), .out15(T15), .sel(Seq));  // open: en
  BUS_Controller bus_controller_1 (
    .IR({IR_15, IR_OUT, B11, B10, B9, B8, B7, B6, B5, B4, B3, B2, B1, B0}), .Seq(Seq), .R(R), .S0(S0),
    .S1(S1), .S2(S2));
  // also tied to GND on the sheet: {AR_OUT[12], AR_OUT[13], AR_OUT[14], AR_OUT[15]}

  // Other names for the same wires on the sheet: IR_OUT (some bits) = {IR_15, B11, B10, B9, B8, B7, B6, B5, B4, B3, B2, B1, B0};
  //   AR_OUT[11:0] = Address

  // Notes on the sheet:
  //   SC
  //   Flip_Flop
  //   Signal_Check
  //   BUS_Controller
endmodule

module I_Controller (
  input  IR_15,
  input  CLK,
  output Indirect
);

  D_Flip_Flop d_ff_1 (.D(IR_15), .clk(CLK), .Q(Indirect));  // open: Qn, preset, reset
endmodule
